# Fritzing sketch Controller_Fritzing_Diagram (saved by Fritzing 0.9.3b)
breadboards: 2

parts:
  U1 = NodeMCU V1.0
  S1 = Pushbutton [package="[THT]"]
  S2 = Pushbutton [package="[THT]"]
  S3 = Pushbutton [package="[THT]"]
  S4 = Pushbutton [package="[THT]"]
  S5 = Pushbutton [package="[THT]"]
  S6 = Pushbutton [package="[THT]"]
  S7 = Pushbutton [package="[THT]"]
  S8 = Pushbutton [package="[THT]"]

nets:
  N1: U1.D1, S6.Pin_3, S6.Pin_4
  N2: U1.D2, S7.Pin_3, S7.Pin_4
  N3: U1.D3, S8.Pin_3, S8.Pin_4
  N4: U1.D4, S1.Pin_3, S1.Pin_4
  N5: U1.3V3, S5.Pin_1, S5.Pin_2
  N6: U1.GND, S1.Pin_1, S1.Pin_2, S2.Pin_1, S2.Pin_2, S3.Pin_1, S3.Pin_2, S4.Pin_1, S4.Pin_2, S4.Pin_3, S4.Pin_4, S6.Pin_1, S6.Pin_2, S7.Pin_1, S7.Pin_2, S8.Pin_1, S8.Pin_2
  N7: U1.D5, S2.Pin_3, S2.Pin_4
  N8: U1.D6, S3.Pin_3, S3.Pin_4
  N9: U1.A0, S5.Pin_3, S5.Pin_4

custom parts:
  NodeMCU V1.0: ESP8266 based NodeMCU
